// Digital circuit N2T_Hack.dig as structural Verilog
module N2T_Hack (
  input  clk
);

  wire Cin, Fout, NA, nand_1_out, nand_2_out, nand_3_out, nand_4_out, nand_5_out, nand_6_out, nand_7_out,
       nand_9_out, nand_10_out, nand_11_out, nand_12_out, nand_13_out, nand_14_out, nand_15_out, nand_16_out,
       nand_17_out, nand_18_out, nand_19_out, nand_20_out, nand_22_out, nand_23_out, nand_24_out,
       nand_25_out, nand_26_out, nand_27_out, nand_28_out, nand_29_out, nand_30_out, nand_31_out,
       nand_32_out, nand_33_out, nand_34_out, nand_35_out, nand_36_out, nand_37_out, nand_38_out,
       nand_39_out, nand_40_out, nand_41_out, nand_42_out, nand_43_out, nand_44_out, nand_45_out,
       nand_46_out, nand_47_out, nand_48_out, nand_49_out, nand_50_out, nand_51_out, nand_52_out,
       nand_53_out, nand_54_out, nand_55_out, nand_56_out, nand_57_out, nand_58_out, nand_59_out,
       nand_60_out, nand_61_out, nand_62_out, nand_63_out, nand_64_out, nand_65_out, nand_66_out,
       nand_67_out, nand_68_out, nand_69_out, nand_70_out, nand_71_out, nand_72_out, nand_73_out,
       nand_74_out, nand_75_out, NB, NO, PCIN, reset_1_out, S_nC, undriven, undriven_2, undriven_3,
       undriven_4, undriven_5, undriven_6, undriven_7, undriven_8, undriven_9, undriven_10, undriven_11,
       undriven_12, undriven_13, undriven_14, undriven_15, ZA, ZB;

  nand nand_1 (nand_1_out, undriven_13, undriven_13);
  nand nand_2 (nand_2_out, PCIN, nand_38_out);
  nand nand_3 (nand_3_out, undriven_14, undriven_13);
  nand nand_4 (nand_4_out, nand_1_out, undriven_15);
  nand nand_5 (nand_5_out, PCIN, nand_2_out);
  nand nand_6 (nand_6_out, nand_2_out, nand_38_out);
  nand nand_7 (nand_7_out, nand_2_out, nand_2_out);
  // NAnd nand_8 has open pins: In_1=nand_3_out, In_2=nand_4_out, out=open
  nand nand_9 (nand_9_out, nand_5_out, nand_6_out);
  nand nand_10 (nand_10_out, undriven_6, undriven_6);
  nand nand_11 (nand_11_out, undriven_7, undriven_7);
  nand nand_12 (nand_12_out, undriven_8, undriven_8);
  nand nand_13 (nand_13_out, nand_34_out, undriven_6);
  nand nand_14 (nand_14_out, nand_10_out, undriven);
  nand nand_15 (nand_15_out, undriven_2, undriven_7);
  nand nand_16 (nand_16_out, nand_11_out, undriven_3);
  nand nand_17 (nand_17_out, undriven_4, undriven_8);
  nand nand_18 (nand_18_out, nand_12_out, undriven_5);
  nand nand_19 (nand_19_out, nand_13_out, nand_14_out);
  nand nand_20 (nand_20_out, nand_15_out, nand_16_out);
  // NAnd nand_21 has open pins: In_1=nand_17_out, In_2=nand_18_out, out=open
  Reset reset_1 (.out(reset_1_out));
  nand nand_22 (nand_22_out, 1'b1, nand_25_out, nand_23_out);
  nand nand_23 (nand_23_out, nand_22_out, clk, reset_1_out);
  nand nand_24 (nand_24_out, nand_23_out, clk, nand_25_out);
  nand nand_25 (nand_25_out, nand_24_out, nand_19_out, reset_1_out);
  nand nand_26 (nand_26_out, 1'b1, nand_29_out, nand_27_out);
  nand nand_27 (nand_27_out, nand_26_out, clk, reset_1_out);
  nand nand_28 (nand_28_out, nand_27_out, clk, nand_29_out);
  nand nand_29 (nand_29_out, nand_28_out, nand_20_out, reset_1_out);
  nand nand_30 (nand_30_out, 1'b1, nand_33_out, nand_31_out);
  nand nand_31 (nand_31_out, nand_30_out, clk, reset_1_out);
  nand nand_32 (nand_32_out, nand_31_out, clk, nand_33_out);
  nand nand_33 (nand_33_out, nand_32_out, undriven_9, reset_1_out);
  nand nand_34 (nand_34_out, 1'b1, nand_23_out, nand_35_out);
  nand nand_35 (nand_35_out, nand_34_out, nand_24_out, reset_1_out);
  nand nand_36 (nand_36_out, 1'b1, nand_27_out, nand_37_out);
  nand nand_37 (nand_37_out, nand_36_out, nand_28_out, reset_1_out);
  nand nand_38 (nand_38_out, 1'b1, nand_31_out, nand_39_out);
  nand nand_39 (nand_39_out, nand_38_out, nand_32_out, reset_1_out);
  nand nand_40 (nand_40_out, undriven_12, undriven_12);
  nand nand_41 (nand_41_out, undriven_10, undriven_12);
  nand nand_42 (nand_42_out, nand_40_out, undriven_11);
  nand nand_43 (nand_43_out, nand_41_out, nand_42_out);
  nand nand_44 (nand_44_out, ZA, ZA);
  nand nand_45 (nand_45_out, ZB, ZB);
  nand nand_46 (nand_46_out, nand_44_out, nand_43_out);
  nand nand_47 (nand_47_out, nand_45_out, nand_36_out);
  nand nand_48 (nand_48_out, nand_46_out, nand_46_out);
  nand nand_49 (nand_49_out, nand_47_out, nand_47_out);
  nand nand_50 (nand_50_out, NA, nand_48_out);
  nand nand_51 (nand_51_out, NB, nand_49_out);
  nand nand_52 (nand_52_out, NA, nand_50_out);
  nand nand_53 (nand_53_out, nand_50_out, nand_48_out);
  nand nand_54 (nand_54_out, NB, nand_51_out);
  nand nand_55 (nand_55_out, nand_51_out, nand_49_out);
  nand nand_56 (nand_56_out, nand_52_out, nand_53_out);
  nand nand_57 (nand_57_out, nand_54_out, nand_55_out);
  nand nand_58 (nand_58_out, nand_56_out, nand_57_out);
  nand nand_59 (nand_59_out, nand_57_out, nand_56_out);
  nand nand_60 (nand_60_out, nand_56_out, nand_58_out);
  nand nand_61 (nand_61_out, nand_58_out, nand_57_out);
  nand nand_62 (nand_62_out, nand_60_out, nand_61_out);
  nand nand_63 (nand_63_out, Cin, nand_62_out);
  nand nand_64 (nand_64_out, nand_62_out, Cin);
  nand nand_65 (nand_65_out, nand_59_out, nand_63_out);
  nand nand_66 (nand_66_out, nand_62_out, nand_64_out);
  nand nand_67 (nand_67_out, nand_64_out, Cin);
  nand nand_68 (nand_68_out, nand_66_out, nand_67_out);
  nand nand_69 (nand_69_out, S_nC, S_nC);
  nand nand_70 (nand_70_out, nand_65_out, S_nC);
  nand nand_71 (nand_71_out, nand_69_out, nand_68_out);
  nand nand_72 (nand_72_out, nand_70_out, nand_71_out);
  nand nand_73 (nand_73_out, NO, nand_72_out);
  nand nand_74 (nand_74_out, NO, nand_73_out);
  nand nand_75 (nand_75_out, nand_73_out, nand_72_out);
  nand nand_76 (Fout, nand_74_out, nand_75_out);
endmodule
