// Digital circuit PC_Incrementer.dig as structural Verilog
module PC_Incrementer (
);

  wire Bout, GCLK, nand_1_out, nand_2_out, nand_3_out, nand_4_out, nand_6_out, nand_7_out, nand_8_out,
       nand_9_out, nand_11_out, nand_12_out, nand_13_out, nand_14_out, nand_16_out, nJMP, nLOAD, PC_Cin,
       PC_Cout, PCin, PCout;

  nand nand_1 (nand_1_out, PCout, PC_Cin);
  nand nand_2 (nand_2_out, PCout, PC_Cin);
  nand nand_3 (nand_3_out, PCout, nand_1_out);
  nand nand_4 (nand_4_out, nand_1_out, PC_Cin);
  nand nand_5 (PC_Cout, nand_2_out, nand_2_out);
  nand nand_6 (nand_6_out, nand_3_out, nand_4_out);
  nand nand_7 (nand_7_out, nJMP, nJMP);
  nand nand_8 (nand_8_out, nand_7_out, Bout);
  nand nand_9 (nand_9_out, nJMP, nand_6_out);
  nand nand_10 (PCin, nand_8_out, nand_9_out);
  nand nand_11 (nand_11_out, nLOAD, nand_14_out, nand_12_out);
  nand nand_12 (nand_12_out, nand_11_out, GCLK, 1'b1);
  nand nand_13 (nand_13_out, nand_12_out, GCLK, nand_14_out);
  nand nand_14 (nand_14_out, nand_13_out, PC_Cout, 1'b1);
  nand nand_15 (PC_Cin, nLOAD, nand_12_out, nand_16_out);
  nand nand_16 (nand_16_out, PC_Cin, nand_13_out, 1'b1);

  // Notes on the sheet:
  //   ALU-PC
  //   Program Counter (Incrementer)
  //   Carry is  set on timeslot T0 of an operation
  //   PC Carry FF
endmodule
