// Digital circuit decode_diode_array.dig as structural Verilog
module decode_diode_array (
  input  IR4,
  input  IR5,
  input  IR6,
  input  nT0,
  input  T1,
  output RESC,
  output SETC,
  output CLR
);

  wire ADD, AND, C, CLA, diodebackward_1_out, diodebackward_6_out, diodebackward_8_out, F, I0, I1, LD, nA,
       nB, nJMP, OR, pullup_1_out, pullup_3_out, pullup_6_out, pullup_7_out, ST, SUB, XOR, xor_1_out, ZERO;

  _74138 U1 (
    .pin1(IR4), .pin2(IR5), .pin3(IR6), .pin4(1'b0), .pin5(1'b0), .pin6(1'b1), .pin7(nJMP), .pin8(1'b0),
    .pin9(ST), .pin10(SUB), .pin11(ADD), .pin12(XOR), .pin13(OR), .pin14(AND), .pin15(LD), .pin16(1'b1));
  DiodeBackward diodebackward_1 (.in(LD), .out(diodebackward_1_out));
  PullUp pullup_1 (.out(pullup_1_out));
  PullUp pullup_2 (.out(diodebackward_1_out));
  DiodeBackward diodebackward_2 (.in(LD), .out(pullup_1_out));
  DiodeBackward diodebackward_3 (.in(ADD), .out(pullup_1_out));
  DiodeBackward diodebackward_4 (.in(SUB), .out(pullup_1_out));
  DiodeBackward diodebackward_5 (.in(nJMP), .out(pullup_1_out));
  PullUp pullup_3 (.out(pullup_3_out));
  DiodeBackward diodebackward_6 (.in(SUB), .out(diodebackward_6_out));
  DiodeBackward diodebackward_7 (.in(SUB), .out(pullup_3_out));
  PullUp pullup_4 (.out(diodebackward_6_out));
  DiodeBackward diodebackward_8 (.in(nJMP), .out(diodebackward_8_out));
  PullUp pullup_5 (.out(diodebackward_8_out));
  PullUp pullup_6 (.out(pullup_6_out));
  DiodeBackward diodebackward_9 (.in(AND), .out(pullup_6_out));
  DiodeBackward diodebackward_10 (.in(OR), .out(pullup_6_out));
  PullUp pullup_7 (.out(pullup_7_out));
  DiodeBackward diodebackward_11 (.in(LD), .out(pullup_7_out));
  DiodeBackward diodebackward_12 (.in(OR), .out(pullup_7_out));
  DiodeBackward diodebackward_13 (.in(XOR), .out(pullup_7_out));
  DiodeBackward diodebackward_14 (.in(ADD), .out(pullup_7_out));
  DiodeBackward diodebackward_15 (.in(SUB), .out(pullup_7_out));
  DiodeBackward diodebackward_16 (.in(ST), .out(pullup_7_out));
  DiodeBackward diodebackward_17 (.in(nJMP), .out(pullup_7_out));
  _74540 U2 (
    .pin1(1'b0), .pin2(pullup_7_out), .pin3(pullup_6_out), .pin4(diodebackward_8_out),
    .pin5(diodebackward_6_out), .pin6(pullup_3_out), .pin7(pullup_1_out), .pin8(diodebackward_1_out),
    .pin9(1'b0), .pin10(1'b0), .pin11(ZERO), .pin12(CLA), .pin13(F), .pin14(C), .pin15(nB), .pin16(nA),
    .pin17(I1), .pin18(I0), .pin19(1'b0), .pin20(1'b1));
  xor xor_1 (xor_1_out, 1'b1, C);
  nand nand_1 (CLR, CLA, nT0);
  nand nand_2 (RESC, nT0, xor_1_out);
  nand nand_3 (SETC, C, T1);

  // Other names for the same wires on the sheet: LOAD = nT0; SETC_t = T1

  // Notes on the sheet:
  //   F
  //   CLA
  //   C
  //   ~B
  //   I1
  //   ~A
  //   I0
  //   LOAD
  //   AND
  //   OR
  //   XOR
  //   ADD
  //   SUB
  //   STORE
  //   JMP
  //   U18
endmodule
